# Fritzing sketch buzzer_with_photocell (saved by Fritzing 0.9.4)
breadboards: 1

parts:
  Part1 = Arduino Uno (Rev3)
  LED1 = LED - 5mm [color="Red (633nm)" package="5 mm [THT]"]
  R1 = Photocell (LDR) [package=THT]
  R2 = Resistor [tolerance=±5% resistance=220 package=THT]
  J1 = Piezo Speaker

nets:
  N1: Part1.A0, R1.pin_0, R2.Pin_1
  N2: Part1.D10_PWM/SS, J1.pin2
  N3: Part1.D13/SCK, LED1.anode
  N4: Part1.5V, R1.pin_1
  N5: Part1.GND, R2.Pin_0, J1.pin1
